# Fritzing sketch Circuit Diagram (saved by Fritzing 0.9.3b)

parts:
  Buzzer1 = Piezo Speaker [part_number="RS 535-8253"]
  Part1 = Adafruit HUZZAH32 ESP32 Feather [part_number="Adafruit #3405"]
  R1 = Resistor [tolerance=±5% resistance=180 package="1206 [SMD]"]
  Momentary_Switch1 = Momentary Switch [package=ksa_sealed_tac_switch]
  R2 = Resistor [tolerance=±5% resistance=12k package="1206 [SMD]"]
  LED1 = RGB LED (com. cathode, rbg) [package="5 mm [THT]"]
  R4 = Resistor [tolerance=±0.1% resistance=1M package="1206 [SMD]"]
  R3 = Resistor [tolerance=±1% resistance=220k package="1206 [SMD]"]

nets:
  N1: Buzzer1.pin2, Part1.GND, R1.Pin_1, Momentary_Switch1.2, R3.Pin_1
  N2: Part1.A0_DAC2, R4.Pin_0, R3.Pin_0
  N3: Part1.3.3V, R2.Pin_1
  N4: Part1.VBAT, R4.Pin_1
  N5: Part1.IO13_A12, LED1.blue_anode
  N6: Part1.IO12_A11, LED1.red_anode
  N7: Part1.IO27_A10, LED1.green_anode
  N8: Part1.IO32_A7, Momentary_Switch1.4
  N9: R1.Pin_0, LED1.common_cathode
  N10: Momentary_Switch1.3, R2.Pin_0

notes:
  Pantri: Pushy
  PB02
  All components should be installed on Adafruit Feather Proto Board & connected to Feather Huzzah using the standard pins that come with the two boards.
  This schematic is shared under the GNU General Public License v3.0.
  www.m-appliances.com
  github.com/m-appliances/Pushy
